// Logisim project UART_Controller.circ as structural Verilog: 1 circuit, main circuit uart
module uart (
  input  clock,
  input  I_Osel,
  input  rd_wr,
  input  [15:0] data,
  input  [7:0] I_Oaddr
);

  wire and_1_out, and_2_out, and_4_out, uart_1_p1, uart_1_p7, uart_1_p8;
  wire [7:0] uart_1_p2, uart_1_p3;

  Pull_Resistor pull_resistor_1 (.node(data[15]));
  Pull_Resistor pull_resistor_2 (.node(data[14]));
  Pull_Resistor pull_resistor_3 (.node(data[13]));
  Pull_Resistor pull_resistor_4 (.node(data[12]));
  Pull_Resistor pull_resistor_5 (.node(data[9]));
  Pull_Resistor pull_resistor_6 (.node(data[11]));
  Pull_Resistor pull_resistor_7 (.node(data[8]));
  Pull_Resistor pull_resistor_8 (.node(data[10]));
  assign data[7:0] = and_1_out ? uart_1_p2 : 8'bz;  // Controlled_Buffer controlled_buffer_1
  and and_1 (and_1_out, rd_wr, uart_1_p8);
  // UART uart_1: pin names not known; wires that end beside it: uart_1_p1, uart_1_p2, uart_1_p3, uart_1_p1, clock, rd_wr, uart_1_p7, uart_1_p8
  and and_2 (and_2_out, ~rd_wr, uart_1_p8);  // AND_Gate
  assign uart_1_p3 = and_2_out ? data[7:0] : 8'bz;  // Controlled_Buffer controlled_buffer_2
  LED led_1 (.in(uart_1_p7));
  and and_3 (uart_1_p8, and_4_out, I_Osel);
  and and_4 (and_4_out, ~I_Oaddr[7], I_Oaddr[6], I_Oaddr[5], I_Oaddr[4], I_Oaddr[3], I_Oaddr[2], ~I_Oaddr[1], ~I_Oaddr[0]);  // AND_Gate

  // Notes on the sheet:
  //   To interrupt arbiter
endmodule
